# Fritzing sketch Number_Plate-Recognition_Prototype_and_Parking_Barrier_Prototype (saved by Fritzing 0.9.3b)
breadboards: 1

parts:
  U1 = ESP32S-HiLetgo [part_number=ESP32S-HiLetgo]
  ESP32_-_Back1 = ESP32 - CAM  # not connected
  J3 = Basic Servo
  YL-83_-_Control_Board2 = YL-83 Rain Sensor - Control Board  # not connected
  YL-83_-_Detection_Board2 = YL-83 Rain Sensor - Detection Board  # not connected

nets:
  N1: U1.3.3, J3.vcc
  GND: U1.GND, J3.gnd
  N2: U1.GPIO18, J3.pulse

custom parts:
  ESP32S-HiLetgo: HiLetgo ESP-WROOM-32 ESP32 ESP-32S Development Board 2.4GHz Dual-Mode WiFi + Bluetooth Dual Cores Microcontroller The ESP32 integrated with Antenna switches, RF Balun, power amplifiers, low-noise amplifiers, filters, and management modules, and the entire solution occupies the least area of PCB. 2.4 GHz Wi-Fi plus Bluetooth dual-mode chip, with TSMC Ultra-low power consumption 40nm technology,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
  ESP32 - CAM: The ESP32-CAM has a very competitive small-size camera module that can operate independently as a minimum system with a footprint of only 27*40.5*4.5mm and a deep sleep current of up to 6mA.
  YL-83 Rain Sensor - Control Board: The YL-83 is a rain sensor that has more resistance when dry and less resistance when wet. The module runs at 5V.
  YL-83 Rain Sensor - Detection Board: The YL-83 is a rain sensor that has more resistance when dry and less resistance when wet. The module runs at 5V.
